// Logisim project ALU.circ as structural Verilog: 4 circuits, main circuit ALU_simple_8bits
module ALU_simple_8bits (
  input  OP,
  input  [7:0] A,
  input  [7:0] B,
  output [7:0] Result,
  output Carry,
  output Overfloww
);

  wire undriven_2;
  wire [7:0] multiplexer_1_out, not_1_out, undriven, xor_1_out;

  assign not_1_out = ~undriven;  // NOT_Gate not_1, 8 bits wide
  // Probe on B
  assign xor_1_out = {8{OP}} ^ B;  // XOR_Gate xor_1, 8 bits wide
  Multiplexer #(.width(8)) multiplexer_1 (.in0(undriven), .in1(not_1_out), .out(multiplexer_1_out), .sel(undriven_2));
  Adder adder_1 (.a(A), .b(xor_1_out), .out(Result), .cin(OP), .cout(Carry));
  Overflow overflow_1 (.A(A[7]), .B(B[7]), .Res(Result[7]), .V(Overfloww));

  // Other names for the same wires on the sheet: Res[7:0] = Result

  // Notes on the sheet:
  //   XOR plus opti que MUX 
  //   Si carry=1 et Overflow=1 =>Overflow négatif 
  //   Si carry=0 et Overflow=1 =>Overflow positif
endmodule

module Overflow (
  input  A,
  input  B,
  input  Res,
  output V
);

  wire and_1_out, and_2_out, not_1_out, not_2_out, not_3_out;

  not not_1 (not_1_out, A);
  not not_2 (not_2_out, B);
  not not_3 (not_3_out, Res);
  and and_1 (and_1_out, not_1_out, not_2_out, Res);
  and and_2 (and_2_out, A, B, not_3_out);
  or or_1 (V, and_1_out, and_2_out);
endmodule

module ALU_complexe_8bits (
  input  [7:0] A,
  input  [7:0] B,
  input  [2:0] OP,
  output C,
  output V,
  output [7:0] Result,
  output N,
  output Z
);

  wire alu_simple_8bits_1_carry;
  wire [7:0] alu_simple_8bits_1_result, and_1_out, not_1_out, or_1_out;

  assign not_1_out = ~A;  // NOT_Gate not_1, 8 bits wide
  assign and_1_out = A & B;  // AND_Gate and_1, 8 bits wide
  assign or_1_out = A | B;  // OR_Gate or_1, 8 bits wide
  ALU_simple_8bits alu_simple_8bits_1 (
    .OP(OP[0]), .A(A), .B(B), .Result(alu_simple_8bits_1_result), .Carry(alu_simple_8bits_1_carry),
    .Overfloww(V));
  Multiplexer #(.select(3), .width(8)) multiplexer_1 (
    .in0(alu_simple_8bits_1_result), .in1(alu_simple_8bits_1_result), .in2({A[6:0], 1'b0}),
    .in3({1'b0, A[7:1]}), .in4({{2{A[7]}}, A[6:1]}), .in5(and_1_out), .in6(or_1_out), .in7(not_1_out),
    .out({N, Result[6:0]}), .sel(OP));
  Multiplexer #(.select(3)) multiplexer_2 (
    .in0(alu_simple_8bits_1_carry), .in1(alu_simple_8bits_1_carry), .in2(A[7]), .in3(A[0]), .in4(A[0]),
    .in5(1'b0), .in6(1'b0), .in7(1'b0), .out(C), .sel(OP));
  nor nor_1 (Z, Result[0], Result[1], Result[2], Result[3], Result[4], Result[5], Result[6], N);

  assign Result[7] = N;

  // Other names for the same wires on the sheet: OP_C[2:0] = OP

  // Notes on the sheet:
  //   Décalage à gauhe
  //   Décalage à droite
  //   Décalage arithmétique à droite
endmodule

module Carry_complexe (
  input  a,
  input  b,
  input  c,
  output Carry
);

  wire and_1_out, not_1_out, not_2_out, not_3_out;

  not not_1 (not_1_out, a);
  not not_2 (not_2_out, b);
  not not_3 (not_3_out, c);
  or or_1 (Carry, not_1_out, and_1_out);
  and and_1 (and_1_out, not_2_out, not_3_out);
endmodule
