// Logisim project Add1bit.circ as structural Verilog: 2 circuits, main circuit Add1bit
module Add1bit (
  input  in_1,
  input  in_2,
  input  in_3,
  output out_4,
  output out_5
);

  wire AND_2_out, AND_3_out, AND_out, XOR_out;

  xor XOR (XOR_out, in_1, in_2);
  and AND (AND_out, in_1, in_2);
  and AND_2 (AND_2_out, in_1, in_3);
  and AND_3 (AND_3_out, in_2, in_3);
  xor XOR_2 (out_4, XOR_out, in_3);
  or OR (out_5, AND_out, AND_2_out, AND_3_out);
endmodule

module Add4bits (
);

  Add1bit add1bit_1 ();  // open: in_1, in_2, in_3, out_4, out_5
  Add1bit add1bit_2 ();  // open: in_1, in_2, in_3, out_4, out_5
  Add1bit add1bit_3 ();  // open: in_1, in_2, in_3, out_4, out_5
  Add1bit add1bit_4 ();  // open: in_1, in_2, in_3, out_4, out_5
endmodule
