// Logisim project Hamming.circ as structural Verilog: 3 circuits, main circuit main
module main (
  input  [3:0] in_1
);

  Codeur codeur_1 ();  // open: a, h6, h5, h4, h3, h2, h1, h0
endmodule

module Codeur (
  input  [3:0] a,
  output h6,
  output h5,
  output h4,
  output h3,
  output h2,
  output h1,
  output h0
);

  wire and_1_out, and_2_out, and_3_out, and_4_out, and_5_out, and_6_out, and_7_out, and_8_out, and_9_out,
       and_10_out, and_11_out, and_12_out, not_1_out, not_2_out, not_3_out, not_4_out;

  not not_1 (not_1_out, a[3]);
  not not_2 (not_2_out, a[2]);
  not not_3 (not_3_out, a[1]);
  not not_4 (not_4_out, a[0]);
  and and_1 (and_1_out, not_1_out, not_2_out, a[1]);
  and and_2 (and_2_out, not_1_out, a[2], not_3_out);
  and and_3 (and_3_out, a[3], not_2_out, not_3_out);
  and and_4 (and_4_out, a[3], a[2], a[1]);
  and and_5 (and_5_out, not_2_out, not_3_out, a[0]);
  and and_6 (and_6_out, not_2_out, a[1], not_4_out);
  and and_7 (and_7_out, a[2], not_3_out, not_4_out);
  and and_8 (and_8_out, a[2], a[1], a[0]);
  and and_9 (and_9_out, not_1_out, not_3_out, a[0]);
  and and_10 (and_10_out, not_1_out, a[1], not_4_out);
  and and_11 (and_11_out, a[3], not_3_out, not_4_out);
  and and_12 (and_12_out, a[3], a[1], a[0]);
  or or_1 (h2, and_1_out, and_2_out, and_3_out, and_4_out);
  or or_2 (h1, and_5_out, and_6_out, and_7_out, and_8_out);
  or or_3 (h0, and_9_out, and_10_out, and_11_out, and_12_out);

  assign h3 = a[0];
  assign h4 = a[1];
  assign h5 = a[2];
  assign h6 = a[3];
endmodule

module decodeur (
  input  h6,
  input  h5,
  input  h4,
  input  h3,
  input  h2,
  input  h1,
  input  h0,
  output [3:0] a,
  output error
);

  wire xor_1_out, xor_2_out, xor_3_out;

  xor xor_1 (xor_1_out, h6, h2);
  xor xor_2 (xor_2_out, h5, h1);
  xor xor_3 (xor_3_out, h4, h0);
  or or_1 (error, xor_1_out, xor_2_out, xor_3_out);

  assign a = {h6, h5, h4, h3};
endmodule
