// Logisim project Labo2.circ as structural Verilog: 3 circuits, main circuit Add1bit
module Add1bit (
  input  A,
  input  B,
  input  C_in,
  output D,
  output C_out
);

  wire and_1_out, AND_2_out, and_3_out, XOR_out;

  xor XOR (XOR_out, A, B);
  and and_1 (and_1_out, A, B);
  and AND_2 (AND_2_out, A, C_in);
  and and_3 (and_3_out, B, C_in);
  xor xor_2 (D, XOR_out, C_in);
  or OR (C_out, and_1_out, AND_2_out, and_3_out);
endmodule

module Add4bits (
  input  C_in,
  input  [3:0] A,
  input  [3:0] B,
  output [3:0] D,
  output C_out
);

  wire add1bit_1_c_out, add1bit_2_c_out, add1bit_3_c_out;

  Add1bit add1bit_1 (.A(A[0]), .B(B[0]), .C_in(C_in), .D(D[0]), .C_out(add1bit_1_c_out));
  Add1bit add1bit_2 (.A(A[1]), .B(B[1]), .C_in(add1bit_1_c_out), .D(D[1]), .C_out(add1bit_2_c_out));
  Add1bit add1bit_3 (.A(A[2]), .B(B[2]), .C_in(add1bit_2_c_out), .D(D[2]), .C_out(add1bit_3_c_out));
  Add1bit add1bit_4 (.A(A[3]), .B(B[3]), .C_in(add1bit_3_c_out), .D(D[3]), .C_out(C_out));
endmodule

module Add8bits (
  input  C_in,
  input  [7:0] A,
  input  [7:0] B,
  output [7:0] D,
  output C_out
);

  wire add4bits_1_c_out;

  Add4bits add4bits_1 (.C_in(C_in), .A(A[3:0]), .B(B[3:0]), .D(D[3:0]), .C_out(add4bits_1_c_out));
  Add4bits add4bits_2 (.C_in(add4bits_1_c_out), .A(A[7:4]), .B(B[7:4]), .D(D[7:4]), .C_out(C_out));
endmodule
