// Logisim project pierre-feuille-ciseau.circ as structural Verilog
module main (
  input  a,
  input  b,
  input  c,
  input  d,
  output L1,
  output L2
);
endmodule

module PierreFeuilleCiseau (
  input  a,
  input  b,
  input  c,
  input  d,
  output L1,
  output L2
);

  wire AD_L1_3_out, AND_L1_1_out, AND_L1_2_out, AND_L1_4_out, AND_L2_1_out, AND_L2_2_out, AND_L2_3_out,
       AND_L2_4_out, not_1_out, not_2_out, not_3_out, not_4_out, not_5_out, not_6_out, not_7_out, not_8_out;

  and AND_L1_1 (AND_L1_1_out, a, c, d);
  not not_1 (not_1_out, b);
  and AND_L1_2 (AND_L1_2_out, a, not_1_out, c);
  not not_2 (not_2_out, a);
  and AD_L1_3 (AD_L1_3_out, not_2_out, b, not_3_out, c);
  not not_3 (not_3_out, d);
  not not_4 (not_4_out, c);
  and AND_L1_4 (AND_L1_4_out, b, not_4_out, d);
  not not_5 (not_5_out, a);
  and AND_L2_1 (AND_L2_1_out, not_5_out, b, d);
  and AND_L2_2 (AND_L2_2_out, a, c, not_6_out);
  not not_6 (not_6_out, d);
  and AND_L2_3 (AND_L2_3_out, b, c, d);
  not not_7 (not_7_out, b);
  and AND_L2_4 (AND_L2_4_out, a, not_7_out, not_8_out, d);
  not not_8 (not_8_out, c);
  or OR_L1 (L1, AND_L1_1_out, AND_L1_2_out, AD_L1_3_out, AND_L1_4_out);
  or OR_L2 (L2, AND_L2_1_out, AND_L2_2_out, AND_L2_3_out, AND_L2_4_out);
endmodule

module PierreFeuilleCiseauAmelioree (
  input  a,
  input  b,
  input  c,
  input  d
);

  wire AD_L1_3_out, AND_L1_1_out, AND_L1_2_out, AND_L1_4_out, AND_L2_1_out, AND_L2_2_out, AND_L2_3_out,
       AND_L2_4_out, not_1_out, not_2_out, not_3_out, not_4_out, not_5_out, not_6_out, not_7_out, not_8_out,
       OR_L1_out, OR_L2_out;
  wire [6:0] septsegementvhdl_1_led_out;

  not not_1 (not_1_out, b);
  not not_2 (not_2_out, a);
  not not_3 (not_3_out, d);
  not not_4 (not_4_out, d);
  not not_5 (not_5_out, b);
  not not_6 (not_6_out, c);
  and AND_L1_1 (AND_L1_1_out, a, c, d);
  and AND_L1_2 (AND_L1_2_out, a, not_1_out, c);
  and AD_L1_3 (AD_L1_3_out, not_2_out, b, not_3_out, c);
  not not_7 (not_7_out, c);
  and AND_L1_4 (AND_L1_4_out, b, not_7_out, d);
  not not_8 (not_8_out, a);
  and AND_L2_1 (AND_L2_1_out, not_8_out, b, d);
  and AND_L2_2 (AND_L2_2_out, a, c, not_4_out);
  and AND_L2_3 (AND_L2_3_out, b, c, d);
  and AND_L2_4 (AND_L2_4_out, a, not_5_out, not_6_out, d);
  or OR_L1 (OR_L1_out, AND_L1_1_out, AND_L1_2_out, AD_L1_3_out, AND_L1_4_out);
  or OR_L2 (OR_L2_out, AND_L2_1_out, AND_L2_2_out, AND_L2_3_out, AND_L2_4_out);
  _7_Segment_Display #(.decimalPoint("false")) Display_out (
    .g(septsegementvhdl_1_led_out[6]), .f(septsegementvhdl_1_led_out[5]), .a(septsegementvhdl_1_led_out[0]),
    .b(septsegementvhdl_1_led_out[1]), .e(septsegementvhdl_1_led_out[4]), .d(septsegementvhdl_1_led_out[3]),
    .c(septsegementvhdl_1_led_out[2]));
  SeptSegementVHDL septsegementvhdl_1 (.l1(OR_L1_out), .l2(OR_L2_out), .LED_out(septsegementvhdl_1_led_out));
endmodule

// VHDL entity SeptSegementVHDL, as the project stores it:
LIBRARY ieee;
USE ieee.std_logic_1164.all;

ENTITY SeptSegementVHDL IS
  PORT (
  ------------------------------------------------------------------------------
  --Insert input ports below
  	l1 		: in 	std_logic;
	l2 		: in 	std_logic;
  ------------------------------------------------------------------------------
  --Insert output ports below
    	LED_out 	: out	std_logic_vector(6 downto 0)
    );
END SeptSegementVHDL;

--------------------------------------------------------------------------------
--Complete your VHDL description below
--------------------------------------------------------------------------------

ARCHITECTURE TypeArchitecture OF SeptSegementVHDL IS

BEGIN
	process(l1, l2)
	begin
		if (l1 = '0' and l2 = '0') then
			LED_out <= "1000000"; -- "-"
		elsif (l1 = '1' and l2 = '0') then
		 	LED_out <= "1110111"; -- "A"
		elsif (l1 = '0' and l2 = '1') then
			LED_out <= "1111100"; -- "B"
		elsif (l1 = '1' and l2 = '1') then
			LED_out <= "1111001"; -- "E" 
		end if;
	end process;

END TypeArchitecture;
