// Logisim project pierre_feuille_ciseau_a.circ as structural Verilog
module main (
  input  a,
  input  b,
  input  c,
  input  d
);

  wire AD_L1_3_out, AND_L1_1_out, AND_L1_2_out, AND_L1_4_out, AND_L2_1_out, AND_L2_2_out, AND_L2_3_out,
       AND_L2_4_out, not_1_out, not_2_out, not_3_out, not_4_out, not_5_out, not_6_out, not_7_out, not_8_out,
       OR_L1_out, OR_L2_out;
  wire [6:0] vhdl_seven_display_1_led_out;

  and AND_L1_1 (AND_L1_1_out, a, c, d);
  not not_1 (not_1_out, b);
  and AND_L1_2 (AND_L1_2_out, a, not_1_out, c);
  not not_2 (not_2_out, a);
  and AD_L1_3 (AD_L1_3_out, not_2_out, b, not_3_out, c);
  not not_3 (not_3_out, d);
  not not_4 (not_4_out, c);
  and AND_L1_4 (AND_L1_4_out, b, not_4_out, d);
  not not_5 (not_5_out, a);
  and AND_L2_1 (AND_L2_1_out, not_5_out, b, d);
  and AND_L2_2 (AND_L2_2_out, a, c, not_6_out);
  not not_6 (not_6_out, d);
  and AND_L2_3 (AND_L2_3_out, b, c, d);
  not not_7 (not_7_out, b);
  and AND_L2_4 (AND_L2_4_out, a, not_7_out, not_8_out, d);
  not not_8 (not_8_out, c);
  or OR_L1 (OR_L1_out, AND_L1_1_out, AND_L1_2_out, AD_L1_3_out, AND_L1_4_out);
  or OR_L2 (OR_L2_out, AND_L2_1_out, AND_L2_2_out, AND_L2_3_out, AND_L2_4_out);
  _7_Segment_Display #(.decimalPoint("false")) Display_out (
    .g(vhdl_seven_display_1_led_out[6]), .f(vhdl_seven_display_1_led_out[5]),
    .a(vhdl_seven_display_1_led_out[0]), .b(vhdl_seven_display_1_led_out[1]),
    .e(vhdl_seven_display_1_led_out[4]), .d(vhdl_seven_display_1_led_out[3]),
    .c(vhdl_seven_display_1_led_out[2]));
  vhdl_seven_display vhdl_seven_display_1 (.l1(OR_L1_out), .l2(OR_L2_out), .LED_out(vhdl_seven_display_1_led_out));
endmodule

// VHDL entity vhdl_seven_display, as the project stores it:
--------------------------------------------------------------------------------
-- Project :
-- File    :
-- Autor   :
-- Date    :
--
--------------------------------------------------------------------------------
-- Description :
--
--------------------------------------------------------------------------------

LIBRARY ieee;
USE ieee.std_logic_1164.all;

ENTITY vhdl_seven_display IS
  PORT (
  ------------------------------------------------------------------------------
  --Insert input ports below
  	l1 		: in 	std_logic;
	l2 		: in 	std_logic;
  ------------------------------------------------------------------------------
  --Insert output ports below
    	LED_out 	: out	std_logic_vector(6 downto 0)
    );
END vhdl_seven_display;

--------------------------------------------------------------------------------
--Complete your VHDL description below
--------------------------------------------------------------------------------

ARCHITECTURE TypeArchitecture OF vhdl_seven_display IS

BEGIN
	process(l1, l2)
	begin
		if (l1 = '0' and l2 = '0') then
			LED_out <= "1000000"; -- "-"
		elsif (l1 = '0' and l2 = '1') then
			LED_out <= "1111100"; -- "B"
		elsif (l1 = '1' and l2 = '0') then
		 	LED_out <= "1110111"; -- "A"
		elsif (l1 = '1' and l2 = '1') then
			LED_out <= "1111001"; -- "E" 
		end if;
	end process;
END TypeArchitecture;
